// Logisim project ALU.circ as structural Verilog: 3 circuits, main circuit Ida ALU
// ALU
module Ida_ALU (
  input  [23:0] ALU_Source_1,
  input  [23:0] ALU_Source_2,
  input  [3:0] Operation,
  output [23:0] ALU_Result
);

  wire [4:0] bit_extender_1_out;
  wire [23:0] Addition, AND, OR, rl, rr, Signed, sll, sra, srl, Subtraction, Unsigned, XOR;

  // Probe on ALU_Source_1
  // Probe on ALU_Source_2
  // Probe on Operation
  // Probe on ALU_Result
  Bit_Extender #(.in_width(24), .out_width(5)) bit_extender_1 (.in(ALU_Source_2), .out(bit_extender_1_out));
  Shifter #(.width(24)) shifter_1 (.in(ALU_Source_1), .\dist (bit_extender_1_out), .out(sll));
  Shifter #(.width(24), .shift("lr")) shifter_2 (.in(ALU_Source_1), .\dist (bit_extender_1_out), .out(srl));
  Shifter #(.width(24), .shift("ar")) shifter_3 (.in(ALU_Source_1), .\dist (bit_extender_1_out), .out(sra));
  Shifter #(.width(24), .shift("rl")) shifter_4 (.in(ALU_Source_1), .\dist (bit_extender_1_out), .out(rl));
  Shifter #(.width(24), .shift("rr")) shifter_5 (.in(ALU_Source_1), .\dist (bit_extender_1_out), .out(rr));
  assign AND = ALU_Source_1 & ALU_Source_2;  // AND_Gate and_1, 24 bits wide
  assign OR = ALU_Source_1 | ALU_Source_2;  // OR_Gate or_1, 24 bits wide
  Adder #(.width(24)) adder_1 (.a(ALU_Source_1), .b(ALU_Source_2), .out(Addition));  // open: cin, cout
  Subtractor #(.width(24)) subtractor_1 (.a(ALU_Source_1), .b(ALU_Source_2), .out(Subtraction));  // open: bin, bout
  Signed_cmp signed_cmp_1 (.input1(ALU_Source_1), .input2(ALU_Source_2), .out_3(Signed));
  Unsigned_cmp unsigned_cmp_1 (.input1(ALU_Source_1), .input2(ALU_Source_2), .out_3(Unsigned));
  assign XOR = ALU_Source_1 ^ ALU_Source_2;  // XOR_Gate xor_1, 24 bits wide
  Multiplexer #(.select(4), .width(24), .enable("false")) multiplexer_1 (
    .in0(sll), .in1(srl), .in2(sra), .in3(rl), .in4(rr), .in5(AND), .in6(OR), .in7(XOR), .in8(Addition),
    .in9(Subtraction), .in10(Addition), .in11(Addition), .in12(Signed), .in13(Unsigned), .in14({24{1'b0}}),
    .in15({24{1'b0}}), .out(ALU_Result), .sel(Operation));

  // Other names for the same wires on the sheet: op[3:0] = Operation; result[23:0] = ALU_Result;
  //   s1[23:0] = ALU_Source_1; s2[23:0] = ALU_Source_2

  // Notes on the sheet:
  //   INPUTS
  //   INPUT PROBES
  //   DO NOT MOVE/ADD/CHANGE ANY INPUT OR OUTPUT PINS!
  //   OUTPUT PROBES
  //   OUTPUT
endmodule

module Signed_cmp (
  input  [23:0] input1,
  input  [23:0] input2,
  output [23:0] out_3
);

  wire comparator_1_eq, comparator_1_lt, comparator_3_eq, comparator_5_eq, comparator_5_gt;
  wire [5:0] or_1_out;

  Comparator #(.width(24), .mode("unsigned")) comparator_1 (
    .a(input1), .b(input2), .eq(comparator_1_eq), .lt(comparator_1_lt));  // open: gt
  Comparator #(.width(24), .mode("unsigned")) comparator_2 (.a(input1), .b(input2), .gt(or_1_out[1]));  // open: eq, lt
  Comparator #(.width(24), .mode("unsigned")) comparator_3 (
    .a(input1), .b(input2), .eq(comparator_3_eq));  // open: gt, lt
  Comparator #(.width(24), .mode("unsigned")) comparator_4 (.a(input1), .b(input2), .eq(or_1_out[3]));  // open: gt, lt
  Comparator #(.width(24), .mode("unsigned")) comparator_5 (
    .a(input1), .b(input2), .gt(comparator_5_gt), .eq(comparator_5_eq));  // open: lt
  Comparator #(.width(24), .mode("unsigned")) comparator_6 (.a(input1), .b(input2), .lt(or_1_out[5]));  // open: gt, eq
  not not_1 (or_1_out[2], comparator_3_eq);
  or or_1 (or_1_out[0], comparator_1_eq, comparator_1_lt);
  or or_2 (or_1_out[4], comparator_5_gt, comparator_5_eq);
  assign out_3 = {{18{1'b0}}, or_1_out};  // Bit_Extender bit_extender_1

  // Notes on the sheet:
  //   ?LE
  //   ?GT
  //   ?NE
  //   ?EQ
  //   ?GE
  //   ?LT
endmodule

module Unsigned_cmp (
  input  [23:0] input1,
  input  [23:0] input2,
  output [23:0] out_3
);

  wire comparator_1_eq, comparator_1_lt, comparator_3_eq, comparator_5_eq, comparator_5_gt;
  wire [5:0] or_1_out;

  Comparator #(.width(24)) comparator_1 (
    .a(input1), .b(input2), .eq(comparator_1_eq), .lt(comparator_1_lt));  // open: gt
  Comparator #(.width(24)) comparator_2 (.a(input1), .b(input2), .gt(or_1_out[1]));  // open: eq, lt
  Comparator #(.width(24)) comparator_3 (.a(input1), .b(input2), .eq(comparator_3_eq));  // open: gt, lt
  Comparator #(.width(24)) comparator_4 (.a(input1), .b(input2), .eq(or_1_out[3]));  // open: gt, lt
  Comparator #(.width(24)) comparator_5 (
    .a(input1), .b(input2), .gt(comparator_5_gt), .eq(comparator_5_eq));  // open: lt
  Comparator #(.width(24)) comparator_6 (.a(input1), .b(input2), .lt(or_1_out[5]));  // open: gt, eq
  not not_1 (or_1_out[2], comparator_3_eq);
  or or_1 (or_1_out[0], comparator_1_eq, comparator_1_lt);
  or or_2 (or_1_out[4], comparator_5_gt, comparator_5_eq);
  assign out_3 = {{18{1'b0}}, or_1_out};  // Bit_Extender bit_extender_1

  // Notes on the sheet:
  //   ?LE
  //   ?GT
  //   ?NE
  //   ?EQ
  //   ?GE
  //   ?LT
endmodule
