// Logisim project CPU.circ as structural Verilog
// CPU
module Ida_CPU (
  input  [31:0] Instruction,
  input  Clock,
  output [23:0] Mem_Data,
  output [23:0] Mem_Address,
  output Mem_Write,
  output [23:0] Next_PC,
  output [23:0] r00,
  output [23:0] r01,
  output [23:0] r02,
  output [23:0] r03,
  output [23:0] r04,
  output [23:0] r05,
  output [23:0] r06,
  output [23:0] r07,
  output [23:0] r08,
  output [23:0] r09,
  output [23:0] r10,
  output [23:0] r11,
  output [23:0] r12,
  output [23:0] r13,
  output [23:0] r14,
  output [23:0] r15
);

  wire and_4_out, and_5_out, cmp, comparator_1_eq, comparator_2_eq, comparator_3_eq, comparator_4_eq,
       comparator_5_eq, comparator_6_eq, comparator_7_eq, comparator_8_eq, comparator_9_eq, comparator_10_eq,
       comparator_10_lt, comparator_11_eq, comparator_12_eq, comparator_13_eq, comparator_14_eq,
       comparator_15_eq, comparator_16_gt, comparator_17_eq, comparator_17_lt, immi, Jump_t, memRead,
       multiplexer_6_out, or_1_out, or_2_out, regWrite;
  wire [2:0] CQ, or_4_out;
  wire [3:0] rd;
  wire [5:0] bit_extender_1_out;
  wire [15:0] bit_extender_2_out;
  wire [19:0] bit_extender_3_out;
  wire [23:0] adder_1_out, bit_extender_4_out, bit_extender_5_out, bit_extender_6_out, cr,
       ida_register_file_1_reg_1_value, ida_register_file_1_reg_2_value, immi_val, immiValue, JUMP,
       multiplexer_2_out, multiplexer_3_out, multiplexer_8_out, multiplexer_9_out, WriteValue, WriteValue_mem;
  wire [31:0] multiplexer_1_out;
  wire [31:28] nextIns;

  // Probe on Instruction
  // Probe on Clock
  // Probe on r00
  // Probe on r01
  // Probe on r02
  // Probe on r03
  // Probe on r04
  // Probe on r05
  // Probe on r06
  // Probe on r07
  // Probe on Mem_Data
  // Probe on Mem_Address
  // Probe on Mem_Write
  // Probe on Next_PC
  Register #(.width(32)) register_1 (
    .D(multiplexer_1_out), .Q({nextIns, CQ, immi, immi_val}), .clk(Clock));  // open: en, clr
  // Probe on r08
  // Probe on r09
  // Probe on r10
  // Probe on r11
  // Probe on r12
  // Probe on r13
  // Probe on r14
  // Probe on r15
  Multiplexer #(.width(32), .enable("false")) multiplexer_1 (
    .in0(Instruction), .in1({32{1'b0}}), .out(multiplexer_1_out), .sel(Jump_t));
  Register #(.width(24)) pc (.D(multiplexer_2_out), .Q(Next_PC), .clk(Clock));  // open: en, clr
  Bit_Extender #(.in_width(24), .out_width(6)) bit_extender_1 (.in(cr), .out(bit_extender_1_out));
  Adder #(.width(24)) adder_1 (.a(24'h1), .b(Next_PC), .out(adder_1_out));  // open: cin, cout
  Comparator #(.width(4), .mode("unsigned")) comparator_1 (
    .a(nextIns), .b(4'b1010), .eq(comparator_1_eq));  // open: gt, lt
  Comparator #(.width(4), .mode("unsigned")) comparator_2 (
    .a(nextIns), .b(4'b1110), .eq(comparator_2_eq));  // open: gt, lt
  Comparator #(.width(1), .mode("unsigned")) comparator_3 (
    .a(1'b1), .b(bit_extender_1_out[0]), .eq(comparator_3_eq));  // open: gt, lt
  Comparator #(.width(1), .mode("unsigned")) comparator_4 (
    .a(1'b1), .b(bit_extender_1_out[1]), .eq(comparator_4_eq));  // open: gt, lt
  Comparator #(.width(1), .mode("unsigned")) comparator_5 (
    .a(1'b1), .b(bit_extender_1_out[2]), .eq(comparator_5_eq));  // open: gt, lt
  Comparator #(.width(1), .mode("unsigned")) comparator_6 (
    .a(1'b1), .b(bit_extender_1_out[3]), .eq(comparator_6_eq));  // open: gt, lt
  Comparator #(.width(1), .mode("unsigned")) comparator_7 (
    .a(1'b1), .b(bit_extender_1_out[4]), .eq(comparator_7_eq));  // open: gt, lt
  Comparator #(.width(1), .mode("unsigned")) comparator_8 (
    .a(1'b1), .b(bit_extender_1_out[5]), .eq(comparator_8_eq));  // open: gt, lt
  Multiplexer #(.width(24), .enable("false")) multiplexer_2 (
    .in0(adder_1_out), .in1(JUMP), .out(multiplexer_2_out), .sel(Jump_t));
  Multiplexer #(.width(24), .enable("false")) multiplexer_3 (
    .in0(Mem_Address), .in1(WriteValue_mem), .out(multiplexer_3_out), .sel(comparator_1_eq));
  Multiplexer #(.width(4), .enable("false")) multiplexer_4 (
    .in0(immi_val[23:20]), .in1(4'b0010), .out(rd), .sel(comparator_2_eq));
  Multiplexer #(.width(24), .enable("false")) multiplexer_5 (
    .in0(multiplexer_3_out), .in1(immiValue), .out(WriteValue), .sel(comparator_9_eq));
  Comparator #(.width(4), .mode("unsigned")) comparator_9 (
    .a(nextIns), .b(4'b1110), .eq(comparator_9_eq));  // open: gt, lt
  Multiplexer #(.select(3), .enable("false")) multiplexer_6 (
    .in0(1'b0), .in1(comparator_3_eq), .in2(comparator_4_eq), .in3(comparator_5_eq), .in4(comparator_6_eq),
    .in5(comparator_7_eq), .in6(comparator_8_eq), .in7(1'b1), .out(multiplexer_6_out), .sel(CQ));
  Comparator #(.width(4), .mode("unsigned")) comparator_10 (
    .a(nextIns), .b(4'b1010), .eq(comparator_10_eq), .lt(comparator_10_lt));  // open: gt
  or or_1 (or_1_out, comparator_10_eq, comparator_10_lt);
  Comparator #(.width(4), .mode("unsigned")) comparator_11 (
    .a(nextIns), .b(4'b1011), .eq(comparator_11_eq));  // open: gt, lt
  Comparator #(.width(4), .mode("unsigned")) comparator_12 (
    .a(nextIns), .b(4'b1100), .eq(comparator_12_eq));  // open: gt, lt
  Comparator #(.width(4), .mode("unsigned")) comparator_13 (
    .a(nextIns), .b(4'b1101), .eq(comparator_13_eq));  // open: gt, lt
  Comparator #(.width(4), .mode("unsigned")) comparator_14 (
    .a(nextIns), .b(4'b1110), .eq(comparator_14_eq));  // open: gt, lt
  Comparator #(.width(4), .mode("unsigned")) comparator_15 (
    .a(nextIns), .b(4'b1111), .eq(comparator_15_eq));  // open: gt, lt
  Ida_Register_File ida_register_file_1 (
    .Read_Reg_1(immi_val[3:0]), .Read_Reg_2(immi_val[19:16]), .Write_Reg(rd), .Write_Value(WriteValue),
    .Reg_1_Value(ida_register_file_1_reg_1_value), .Reg_2_Value(ida_register_file_1_reg_2_value),
    .Reg_Write(regWrite), .Clock(Clock), .r00(r00), .r01(r01), .r02(r02), .r03(r03), .r04(r04), .r05(r05),
    .r06(r06), .r07(r07), .r08(r08), .r09(r09), .r10(r10), .r11(r11), .r12(r12), .r13(r13), .r14(r14),
    .r15(r15), .Reg_3_Value(Mem_Data));
  or or_2 (or_2_out, comparator_12_eq, comparator_13_eq);
  and and_1 (cmp, multiplexer_6_out, or_2_out);
  Comparator #(.width(4), .mode("unsigned")) comparator_16 (
    .a(nextIns), .b(4'b1011), .gt(comparator_16_gt));  // open: eq, lt
  and and_2 (memRead, multiplexer_6_out, comparator_10_eq);
  and and_3 (Mem_Write, multiplexer_6_out, comparator_11_eq);
  and and_4 (and_4_out, multiplexer_6_out, or_1_out);
  and and_5 (and_5_out, multiplexer_6_out, comparator_14_eq);
  and and_6 (Jump_t, multiplexer_6_out, comparator_15_eq);
  Multiplexer #(.width(24), .enable("false")) multiplexer_7 (
    .in0(ida_register_file_1_reg_1_value), .in1(immiValue), .out(JUMP), .sel(immi));
  Multiplexer #(.width(24), .enable("false")) multiplexer_8 (
    .in0(ida_register_file_1_reg_2_value), .in1(Mem_Data), .out(multiplexer_8_out), .sel(comparator_16_gt));
  or or_3 (regWrite, and_4_out, and_5_out);
  Ida_ALU ida_alu_1 (
    .ALU_Source_1(multiplexer_8_out), .ALU_Source_2(JUMP), .Operation(nextIns), .ALU_Result(Mem_Address));
  Multiplexer #(.width(24), .enable("false")) multiplexer_9 (
    .in0(cr), .in1(Mem_Address), .out(multiplexer_9_out), .sel(cmp));
  Comparator #(.width(4), .mode("unsigned")) comparator_17 (
    .a(nextIns), .b(4'b1011), .eq(comparator_17_eq), .lt(comparator_17_lt));  // open: gt
  Comparator #(.width(4), .mode("unsigned")) comparator_18 (
    .a(nextIns), .b(4'b1100), .eq(or_4_out[1]));  // open: gt, lt
  Comparator #(.width(4), .mode("unsigned")) comparator_19 (
    .a(nextIns), .b(4'b1101), .eq(or_4_out[2]));  // open: gt, lt
  Register #(.width(24)) register_2 (.D(multiplexer_9_out), .Q(cr), .clk(Clock));  // open: en, clr
  RAM #(.addrWidth(24), .dataWidth(24), .bus("separate")) ram_1 (
    .addr(Mem_Address), .din(Mem_Data), .data(WriteValue_mem), .str(Mem_Write), .clk(Clock), .ld(memRead));  // open: sel, clr
  or or_4 (or_4_out[0], comparator_17_eq, comparator_17_lt);
  Bit_Extender #(.in_width(24)) bit_extender_2 (.in(immi_val), .out(bit_extender_2_out));
  Bit_Extender #(.in_width(24), .out_width(20)) bit_extender_3 (.in(immi_val), .out(bit_extender_3_out));
  assign bit_extender_4_out = {{8{bit_extender_2_out[15]}}, bit_extender_2_out};  // Bit_Extender bit_extender_4
  assign bit_extender_5_out = {{4{bit_extender_3_out[19]}}, bit_extender_3_out};  // Bit_Extender bit_extender_5
  assign bit_extender_6_out = {{4{1'b0}}, bit_extender_3_out};  // Bit_Extender bit_extender_6
  Multiplexer #(.select(3), .width(24), .enable("false")) multiplexer_10 (
    .in0(immi_val), .in1(bit_extender_4_out), .in2(bit_extender_5_out), .in4(bit_extender_6_out),
    .out(immiValue), .sel(or_4_out));  // open: in3, in5, in6, in7

  // Other names for the same wires on the sheet: clk = Clock; inst[31:0] = Instruction; memData[23:0] = Mem_Data;
  //   RDVALUE[23:0] = Mem_Data; memWrite = Mem_Write; nextIns[27:0] = {CQ, immi, immi_val}; ri[3:0] = immi_val[3:0];
  //   rs[3:0] = immi_val[19:16]; op[3:0] = nextIns; nextPC[23:0] = Next_PC; memAddr[23:0] = Mem_Address;
  //   output[23:0] = Mem_Address

  // Notes on the sheet:
  //   INPUTS
  //   pipeline
  //   INPUT PROBES
  //   OUTPUT PROBES
  //   OUTPUTS
  //   DO NOT MOVE/ADD/CHANGE ANY INPUT OR OUTPUT PINS!
  //   Next PC
  //   Decode
  //   Value store from LOAD or calculation
  //   ?NO
  //   ?LE
  //   ?GT
  //   ?NE
  //   ?EQ
  //   ?GE
  //   ?LT
  //   ?OK
  //   ri
  //   rs
  //   rd
  //   *Note: Spec didn't say we MUST change the instruction to NOP
  //   Instead change the instruction nop, we turn off all controls so it bascially does samething as nop
  //   A3
  //   A2
  //   A2
  //   Immidiate Sign Extension
endmodule

module pipeline (
  input  clk,
  input  reset,
  input  [23:0] w0,
  input  [23:0] w1,
  input  [23:0] w2,
  input  [23:0] w3,
  input  [23:0] w4,
  input  [23:0] w5,
  input  [23:0] w6,
  input  [23:0] w7,
  input  [23:0] w8,
  input  [23:0] w9,
  input  [23:0] w10,
  input  [23:0] w11,
  input  [23:0] w12,
  input  [23:0] w13,
  input  [23:0] w14,
  input  [23:0] w15,
  output [23:0] r0,
  output [23:0] r1,
  output [23:0] r2,
  output [23:0] r3,
  output [23:0] r4,
  output [23:0] r5,
  output [23:0] r6,
  output [23:0] r7,
  output [23:0] r8,
  output [23:0] r9,
  output [23:0] r10,
  output [23:0] r11,
  output [23:0] r12,
  output [23:0] r13,
  output [23:0] r14,
  output [23:0] r15
);

  Register #(.width(24)) register_1 (.D(w0), .Q(r0), .clk(clk), .clr(reset));  // open: en
  Register #(.width(24)) register_2 (.D(w1), .Q(r1), .clk(clk), .clr(reset));  // open: en
  Register #(.width(24)) register_3 (.D(w2), .Q(r2), .clk(clk), .clr(reset));  // open: en
  Register #(.width(24)) register_4 (.D(w3), .Q(r3), .clk(clk), .clr(reset));  // open: en
  Register #(.width(24)) register_5 (.D(w4), .Q(r4), .clk(clk), .clr(reset));  // open: en
  Register #(.width(24)) register_6 (.D(w5), .Q(r5), .clk(clk), .clr(reset));  // open: en
  Register #(.width(24)) register_7 (.D(w6), .Q(r6), .clk(clk), .clr(reset));  // open: en
  Register #(.width(24)) register_8 (.D(w7), .Q(r7), .clk(clk), .clr(reset));  // open: en
  Register #(.width(24)) register_9 (.D(w8), .Q(r8), .clk(clk), .clr(reset));  // open: en
  Register #(.width(24)) register_10 (.D(w9), .Q(r9), .clk(clk), .clr(reset));  // open: en
  Register #(.width(24)) register_11 (.D(w10), .Q(r10), .clk(clk), .clr(reset));  // open: en
  Register #(.width(24)) register_12 (.D(w11), .Q(r11), .clk(clk), .clr(reset));  // open: en
  Register #(.width(24)) register_13 (.D(w12), .Q(r12), .clk(clk), .clr(reset));  // open: en
  Register #(.width(24)) register_14 (.D(w13), .Q(r13), .clk(clk), .clr(reset));  // open: en
  Register #(.width(24)) register_15 (.D(w14), .Q(r14), .clk(clk), .clr(reset));  // open: en
  Register #(.width(24)) register_16 (.D(w15), .Q(r15), .clk(clk), .clr(reset));  // open: en
endmodule
