// Logisim project REG.circ as structural Verilog: 1 circuit, main circuit Ida Register File
// Register File
module Ida_Register_File (
  input  [3:0] Read_Reg_1,
  input  [3:0] Read_Reg_2,
  input  [3:0] Write_Reg,
  input  [23:0] Write_Value,
  input  Reg_Write,
  input  Clock,
  output [23:0] Reg_1_Value,
  output [23:0] Reg_2_Value,
  output [23:0] Reg_3_Value,
  output [23:0] r00,
  output [23:0] r01,
  output [23:0] r02,
  output [23:0] r03,
  output [23:0] r04,
  output [23:0] r05,
  output [23:0] r06,
  output [23:0] r07,
  output [23:0] r08,
  output [23:0] r09,
  output [23:0] r10,
  output [23:0] r11,
  output [23:0] r12,
  output [23:0] r13,
  output [23:0] r14,
  output [23:0] r15
);

  wire demultiplexer_1_out1, demultiplexer_1_out2, demultiplexer_1_out3, demultiplexer_1_out4,
       demultiplexer_1_out5, demultiplexer_1_out6, demultiplexer_1_out7, demultiplexer_1_out8,
       demultiplexer_1_out9, demultiplexer_1_out10, demultiplexer_1_out11, demultiplexer_1_out12,
       demultiplexer_1_out13, demultiplexer_1_out14, demultiplexer_1_out15;
  wire [23:0] multiplexer_4_out, multiplexer_5_out, multiplexer_6_out, multiplexer_7_out, multiplexer_8_out,
       multiplexer_9_out, multiplexer_10_out, multiplexer_11_out, multiplexer_12_out, multiplexer_13_out,
       multiplexer_14_out, multiplexer_15_out, multiplexer_16_out, multiplexer_17_out, multiplexer_18_out;

  // Probe on Read_Reg_1
  // Probe on Read_Reg_2
  // Probe on Write_Reg
  // Probe on Write_Value
  // Probe on Reg_Write
  // Probe on Clock
  // Probe on Reg_1_Value
  // Probe on Reg_2_Value
  // Probe on Reg_3_Value
  // Probe on {24{1'b0}}
  // Probe on r01
  // Probe on r02
  // Probe on r03
  // Probe on r04
  // Probe on r05
  // Probe on r06
  // Probe on r07
  // Probe on r08
  // Probe on r09
  // Probe on r10
  // Probe on r11
  // Probe on r12
  // Probe on r13
  // Probe on r14
  // Probe on r15
  Multiplexer #(.select(4), .width(24), .enable("false")) multiplexer_1 (
    .in0({24{1'b0}}), .in1(r01), .in2(r02), .in3(r03), .in4(r04), .in5(r05), .in6(r06), .in7(r07), .in8(r08),
    .in9(r09), .in10(r10), .in11(r11), .in12(r12), .in13(r13), .in14(r14), .in15(r15), .out(Reg_1_Value),
    .sel(Read_Reg_1));
  Multiplexer #(.select(4), .width(24), .enable("false")) multiplexer_2 (
    .in0({24{1'b0}}), .in1(r01), .in2(r02), .in3(r03), .in4(r04), .in5(r05), .in6(r06), .in7(r07), .in8(r08),
    .in9(r09), .in10(r10), .in11(r11), .in12(r12), .in13(r13), .in14(r14), .in15(r15), .out(Reg_2_Value),
    .sel(Read_Reg_2));
  Multiplexer #(.select(4), .width(24), .enable("false")) multiplexer_3 (
    .in0({24{1'b0}}), .in1(r01), .in2(r02), .in3(r03), .in4(r04), .in5(r05), .in6(r06), .in7(r07), .in8(r08),
    .in9(r09), .in10(r10), .in11(r11), .in12(r12), .in13(r13), .in14(r14), .in15(r15), .out(Reg_3_Value),
    .sel(Write_Reg));
  Multiplexer #(.width(24), .enable("false")) multiplexer_4 (
    .in0(r01), .in1(Write_Value), .out(multiplexer_4_out), .sel(demultiplexer_1_out1));
  Multiplexer #(.width(24), .enable("false")) multiplexer_5 (
    .in0(r02), .in1(Write_Value), .out(multiplexer_5_out), .sel(demultiplexer_1_out2));
  Multiplexer #(.width(24), .enable("false")) multiplexer_6 (
    .in0(r03), .in1(Write_Value), .out(multiplexer_6_out), .sel(demultiplexer_1_out3));
  Multiplexer #(.width(24), .enable("false")) multiplexer_7 (
    .in0(r04), .in1(Write_Value), .out(multiplexer_7_out), .sel(demultiplexer_1_out4));
  Multiplexer #(.width(24), .enable("false")) multiplexer_8 (
    .in0(r05), .in1(Write_Value), .out(multiplexer_8_out), .sel(demultiplexer_1_out5));
  Multiplexer #(.width(24), .enable("false")) multiplexer_9 (
    .in0(r06), .in1(Write_Value), .out(multiplexer_9_out), .sel(demultiplexer_1_out6));
  Multiplexer #(.width(24), .enable("false")) multiplexer_10 (
    .in0(r07), .in1(Write_Value), .out(multiplexer_10_out), .sel(demultiplexer_1_out7));
  Multiplexer #(.width(24), .enable("false")) multiplexer_11 (
    .in0(r08), .in1(Write_Value), .out(multiplexer_11_out), .sel(demultiplexer_1_out8));
  Multiplexer #(.width(24), .enable("false")) multiplexer_12 (
    .in0(r09), .in1(Write_Value), .out(multiplexer_12_out), .sel(demultiplexer_1_out9));
  Multiplexer #(.width(24), .enable("false")) multiplexer_13 (
    .in0(r10), .in1(Write_Value), .out(multiplexer_13_out), .sel(demultiplexer_1_out10));
  Multiplexer #(.width(24), .enable("false")) multiplexer_14 (
    .in0(r11), .in1(Write_Value), .out(multiplexer_14_out), .sel(demultiplexer_1_out11));
  Multiplexer #(.width(24), .enable("false")) multiplexer_15 (
    .in0(r12), .in1(Write_Value), .out(multiplexer_15_out), .sel(demultiplexer_1_out12));
  Multiplexer #(.width(24), .enable("false")) multiplexer_16 (
    .in0(r13), .in1(Write_Value), .out(multiplexer_16_out), .sel(demultiplexer_1_out13));
  Multiplexer #(.width(24), .enable("false")) multiplexer_17 (
    .in0(r14), .in1(Write_Value), .out(multiplexer_17_out), .sel(demultiplexer_1_out14));
  Multiplexer #(.width(24), .enable("false")) multiplexer_18 (
    .in0(r15), .in1(Write_Value), .out(multiplexer_18_out), .sel(demultiplexer_1_out15));
  Register #(.width(24)) register_1 (.D(multiplexer_4_out), .Q(r01), .clk(Clock));  // open: en, clr
  Register #(.width(24)) register_2 (.D(multiplexer_5_out), .Q(r02), .clk(Clock));  // open: en, clr
  Register #(.width(24)) register_3 (.D(multiplexer_6_out), .Q(r03), .clk(Clock));  // open: en, clr
  Register #(.width(24)) register_4 (.D(multiplexer_7_out), .Q(r04), .clk(Clock));  // open: en, clr
  Register #(.width(24)) register_5 (.D(multiplexer_8_out), .Q(r05), .clk(Clock));  // open: en, clr
  Register #(.width(24)) register_6 (.D(multiplexer_9_out), .Q(r06), .clk(Clock));  // open: en, clr
  Register #(.width(24)) register_7 (.D(multiplexer_10_out), .Q(r07), .clk(Clock));  // open: en, clr
  Register #(.width(24)) register_8 (.D(multiplexer_11_out), .Q(r08), .clk(Clock));  // open: en, clr
  Register #(.width(24)) register_9 (.D(multiplexer_12_out), .Q(r09), .clk(Clock));  // open: en, clr
  Register #(.width(24)) register_10 (.D(multiplexer_13_out), .Q(r10), .clk(Clock));  // open: en, clr
  Register #(.width(24)) register_11 (.D(multiplexer_14_out), .Q(r11), .clk(Clock));  // open: en, clr
  Register #(.width(24)) register_12 (.D(multiplexer_15_out), .Q(r12), .clk(Clock));  // open: en, clr
  Register #(.width(24)) register_13 (.D(multiplexer_16_out), .Q(r13), .clk(Clock));  // open: en, clr
  Register #(.width(24)) register_14 (.D(multiplexer_17_out), .Q(r14), .clk(Clock));  // open: en, clr
  Register #(.width(24)) register_15 (.D(multiplexer_18_out), .Q(r15), .clk(Clock));  // open: en, clr
  Demultiplexer #(.select(4)) demultiplexer_1 (
    .out1(demultiplexer_1_out1), .out2(demultiplexer_1_out2), .out3(demultiplexer_1_out3),
    .out4(demultiplexer_1_out4), .out5(demultiplexer_1_out5), .out6(demultiplexer_1_out6),
    .out7(demultiplexer_1_out7), .out8(demultiplexer_1_out8), .out9(demultiplexer_1_out9),
    .out10(demultiplexer_1_out10), .out11(demultiplexer_1_out11), .out12(demultiplexer_1_out12),
    .out13(demultiplexer_1_out13), .out14(demultiplexer_1_out14), .out15(demultiplexer_1_out15), .in(1'b1),
    .sel(Write_Reg), .en(Reg_Write));  // open: out0

  assign r00 = {24{1'b0}};

  // Other names for the same wires on the sheet: clk = Clock; reg1Read[3:0] = Read_Reg_1; reg1Val[23:0] = Reg_1_Value;
  //   reg2Read[3:0] = Read_Reg_2; reg2Val[23:0] = Reg_2_Value; reg3Val[23:0] = Reg_3_Value;
  //   reg3Write[3:0] = Write_Reg; write = Reg_Write; writeVal[23:0] = Write_Value

  // Notes on the sheet:
  //   INPUT PINS
  //   INPUT PROBES
  //   OUTPUT PROBES
  //   OUTPUT PINS
  //   DO NOT MOVE/ADD/CHANGE ANY INPUT OR OUTPUT PINS!
  //   Read
  //   Write
endmodule
